// Logisim project 2lista24h.circ as structural Verilog
module _3 (
  input  x1,
  input  x2,
  input  x3,
  input  x4,
  input  x5,
  input  y1,
  input  y2,
  input  y3,
  input  y4,
  input  y5,
  output out_11
);

  wire xnor_1_out, xnor_2_out, xnor_3_out, xnor_4_out, xnor_5_out;

  xnor xnor_1 (xnor_1_out, x5, y5);
  xnor xnor_2 (xnor_2_out, x4, y4);
  xnor xnor_3 (xnor_3_out, x3, y3);
  xnor xnor_4 (xnor_4_out, x2, y2);
  xnor xnor_5 (xnor_5_out, x1, y1);
  nand nand_1 (out_11, xnor_5_out, xnor_4_out, xnor_3_out, xnor_2_out, xnor_1_out);
endmodule

module _4 (
  input  A,
  input  B,
  input  C,
  input  D,
  input  E,
  output P,
  output out_7,
  output out_8,
  output out_9,
  output out_10,
  output out_11
);

  wire xor_1_out, xor_2_out, xor_3_out;

  xor xor_1 (xor_1_out, A, B);
  xor xor_2 (xor_2_out, C, D);
  xor xor_3 (xor_3_out, xor_1_out, xor_2_out);
  xnor xnor_1 (P, xor_3_out, E);

  assign out_7 = A;
  assign out_8 = B;
  assign out_9 = C;
  assign out_10 = D;
  assign out_11 = E;
endmodule

module _6 (
  input  A,
  input  B,
  output X,
  output Y
);

  wire not_1_out;

  and and_1 (X, A, B);
  not not_1 (not_1_out, B);
  and and_2 (Y, not_1_out, A);
endmodule

module _7 (
  input  A,
  input  B,
  input  C,
  output S
);

  wire and_1_out;

  and and_1 (and_1_out, B, C);
  and and_2 (S, A, and_1_out);
endmodule

module _8 (
  input  A,
  input  B,
  input  C,
  output S
);

  wire xor_1_out;

  xor xor_1 (xor_1_out, B, C);
  nand nand_1 (S, A, xor_1_out);
endmodule

module _9 (
  input  in_1,
  input  in_2,
  output out_3
);

  xor xor_1 (out_3, in_1, in_2);
endmodule
