// Logisim project circuitDisplay.circ as structural Verilog: 9 circuits, main circuit main
module main (
  input  in_1,
  input  in_2
);

  wire a_out_4, b_out_4, c_out_4, d_out_4, e_out_4, f_out_4, g_out_4, t_ff_1_q, t_ff_1_qn, t_ff_2_q,
       t_ff_2_qn, t_ff_3_q;

  T_Flip_Flop t_ff_1 (.clk(in_1), .T(in_2), .Q(t_ff_1_q), .Qn(t_ff_1_qn));  // open: preset, reset, en
  T_Flip_Flop t_ff_2 (.clk(t_ff_1_qn), .T(in_2), .Q(t_ff_2_q), .Qn(t_ff_2_qn));  // open: preset, reset, en
  T_Flip_Flop t_ff_3 (.clk(t_ff_2_qn), .T(in_2), .Q(t_ff_3_q));  // open: Qn, preset, reset, en
  a a (.A(t_ff_3_q), .B(t_ff_2_q), .C(t_ff_1_q), .out_4(a_out_4));
  b b (.A(t_ff_3_q), .B(t_ff_2_q), .C(t_ff_1_q), .out_4(b_out_4));
  c c (.A(t_ff_3_q), .B(t_ff_2_q), .C(t_ff_1_q), .out_4(c_out_4));
  d d (.A(t_ff_3_q), .B(t_ff_2_q), .C(t_ff_1_q), .out_4(d_out_4));
  e e (.A(t_ff_3_q), .B(t_ff_2_q), .C(t_ff_1_q), .out_4(e_out_4));
  f f (.A(t_ff_3_q), .B(t_ff_2_q), .C(t_ff_1_q), .out_4(f_out_4));
  g g (.A(t_ff_3_q), .B(t_ff_2_q), .C(t_ff_1_q), .out_4(g_out_4));
  _7_Segment_Display u_7_segment_display_1 (
    .g(g_out_4), .f(f_out_4), .a(a_out_4), .b(b_out_4), .e(e_out_4), .d(d_out_4), .c(c_out_4));  // open: dp
endmodule

module b (
  input  A,
  input  B,
  input  C,
  output out_4
);

  wire not_1_out, xnor_1_out;

  not not_1 (not_1_out, A);
  xnor xnor_1 (xnor_1_out, B, C);
  or or_1 (out_4, not_1_out, xnor_1_out);
endmodule

module a (
  input  A,
  input  B,
  input  C,
  output out_4
);

  wire xnor_1_out;

  xnor xnor_1 (xnor_1_out, A, C);
  or or_1 (out_4, xnor_1_out, B);
endmodule

module c (
  input  A,
  input  B,
  input  C,
  output out_4
);

  wire not_1_out;

  not not_1 (not_1_out, B);
  or or_1 (out_4, A, not_1_out, C);
endmodule

module d (
  input  A,
  input  B,
  input  C,
  output out_4
);

  wire and_1_out, and_2_out, and_3_out, and_4_out, not_1_out, not_2_out, not_3_out, not_4_out, not_5_out,
       not_6_out;

  not not_1 (not_1_out, A);
  not not_2 (not_2_out, C);
  not not_3 (not_3_out, B);
  not not_4 (not_4_out, C);
  not not_5 (not_5_out, A);
  not not_6 (not_6_out, B);
  and and_1 (and_1_out, not_1_out, B);
  and and_2 (and_2_out, not_2_out, B);
  and and_3 (and_3_out, not_3_out, not_4_out, not_5_out);
  and and_4 (and_4_out, not_6_out, C, A);
  or or_1 (out_4, and_1_out, and_2_out, and_3_out, and_4_out);
endmodule

module e (
  input  A,
  input  B,
  input  C,
  output out_4
);

  wire and_1_out, and_2_out, not_1_out, not_2_out;

  not not_1 (not_1_out, A);
  not not_2 (not_2_out, C);
  and and_1 (and_1_out, not_1_out, not_2_out);
  and and_2 (and_2_out, not_2_out, B);
  or or_1 (out_4, and_1_out, and_2_out);
endmodule

module f (
  input  A,
  input  B,
  input  C,
  output out_4
);

  wire and_1_out, and_2_out, and_3_out, not_1_out, not_2_out, not_3_out, not_4_out;

  not not_1 (not_1_out, B);
  not not_2 (not_2_out, C);
  not not_3 (not_3_out, A);
  not not_4 (not_4_out, B);
  and and_1 (and_1_out, A, not_1_out);
  and and_2 (and_2_out, not_2_out, A, B);
  and and_3 (and_3_out, not_2_out, not_3_out, not_4_out);
  or or_1 (out_4, and_1_out, and_2_out, and_3_out);
endmodule

module g (
  input  A,
  input  B,
  input  C,
  output out_4
);

  wire and_1_out, and_2_out, and_3_out, not_1_out, not_2_out, not_3_out;

  not not_1 (not_1_out, A);
  not not_2 (not_2_out, C);
  not not_3 (not_3_out, B);
  and and_1 (and_1_out, not_1_out, B);
  and and_2 (and_2_out, not_2_out, A);
  and and_3 (and_3_out, not_3_out, A);
  or or_1 (out_4, and_1_out, and_2_out, and_3_out);
endmodule

module _1 (
  input  in_1,
  input  in_2,
  output out_3,
  output out_4,
  output out_5
);

  wire t_ff_1_qn, t_ff_2_qn;

  T_Flip_Flop t_ff_1 (.clk(in_1), .T(in_2), .Q(out_5), .Qn(t_ff_1_qn));  // open: preset, reset, en
  T_Flip_Flop t_ff_2 (.clk(t_ff_1_qn), .T(in_2), .Q(out_4), .Qn(t_ff_2_qn));  // open: preset, reset, en
  T_Flip_Flop t_ff_3 (.clk(t_ff_2_qn), .T(in_2), .Q(out_3));  // open: Qn, preset, reset, en
endmodule
