// Logisim project full-adder.circ as structural Verilog: 5 circuits, main circuit main
module main (
  input  Cin,
  input  A,
  input  B,
  output Sum,
  output Cout
);

  wire half_adder_1_cout, half_adder_1_s, half_adder_2_cout;

  half_adder half_adder_1 (.A(A), .B(B), .S(half_adder_1_s), .Cout(half_adder_1_cout));
  half_adder half_adder_2 (.A(Cin), .B(half_adder_1_s), .S(Sum), .Cout(half_adder_2_cout));
  or or_1 (Cout, half_adder_2_cout, half_adder_1_cout);
endmodule

module half_adder (
  input  A,
  input  B,
  output S,
  output Cout
);

  xor xor_1 (S, A, B);
  and and_1 (Cout, B, A);
endmodule

module full_adder (
  input  Cin,
  input  A,
  input  B,
  input  in_4,
  input  in_5,
  output Sum,
  output Cout,
  output out_8,
  output out_9
);

  wire half_adder_1_cout, half_adder_1_s, half_adder_3_cout;

  half_adder half_adder_1 (.A(A), .B(B), .S(half_adder_1_s), .Cout(half_adder_1_cout));
  half_adder half_adder_2 (.A(in_4), .B(in_5), .S(out_8), .Cout(out_9));
  half_adder half_adder_3 (.A(Cin), .B(half_adder_1_s), .S(Sum), .Cout(half_adder_3_cout));
  or or_1 (Cout, half_adder_3_cout, half_adder_1_cout);
endmodule

module half_subtractor (
  input  A,
  input  B,
  output Difference,
  output Carry
);

  wire not_1_out;

  not not_1 (not_1_out, A);
  xor xor_1 (Difference, A, B);
  and and_1 (Carry, B, not_1_out);
endmodule

module full_subtractor (
  input  Cin,
  input  A,
  input  B,
  output Difference,
  output Cout
);

  wire half_subtractor_1_carry, half_subtractor_1_difference, half_subtractor_2_carry;

  half_subtractor half_subtractor_1 (
    .A(A), .B(B), .Difference(half_subtractor_1_difference), .Carry(half_subtractor_1_carry));
  half_subtractor half_subtractor_2 (
    .A(Cin), .B(half_subtractor_1_difference), .Difference(Difference), .Carry(half_subtractor_2_carry));
  and and_1 (Cout, half_subtractor_2_carry, half_subtractor_1_carry);
endmodule
