// Logisim project lista_01.circ as structural Verilog: 1 circuit, main circuit main
module main (
  input  in_1,
  input  I,
  input  in_3,
  input  F,
  input  P,
  input  b,
  input  in_7,
  input  I_2,
  input  F_2,
  input  P_2,
  output out_11,
  output out_12,
  output out_13,
  output out_14
);

  wire nand_1_out, nor_1_out, nor_3_out, not_1_out, or_1_out;

  not not_1 (not_1_out, I_2);
  or or_1 (or_1_out, F_2, P_2);
  nand nand_1 (nand_1_out, in_1, in_3);
  nor nor_1 (nor_1_out, b, in_7);
  nand nand_2 (out_11, nand_1_out, nand_1_out);
  nor nor_2 (out_13, nor_1_out, nor_1_out);
  and and_1 (out_14, not_1_out, or_1_out);
  nor nor_3 (nor_3_out, F, P);
  nor nor_4 (out_12, I, nor_3_out);

  // Notes on the sheet:
  //   (1) a)
  //   (3)
  //   Farol
  //   Ignição
  //   Porta
  //   1
  //   ligado
  //   ligada
  //   aberta
  //   0
  //   desligado
  //   desligada
  //   fechada
  //   (4)
endmodule
