// Logisim project lista_04.circ as structural Verilog: 4 circuits, main circuit 1
module _1 (
  input  in_1,
  input  in_2,
  input  in_3,
  input  in_4,
  input  in_5,
  input  in_6,
  input  in_7,
  input  in_8,
  input  P,
  output P_2,
  output out_11,
  output out_12,
  output out_13,
  output out_14,
  output out_15
);

  wire xor_1_out, xor_2_out, xor_3_out, xor_4_out, xor_6_out;

  xor xor_1 (xor_1_out, in_1, in_2);
  xor xor_2 (xor_2_out, in_3, in_4);
  xor xor_3 (xor_3_out, in_5, in_6);
  xor xor_4 (xor_4_out, in_7, in_8);
  xor xor_5 (P_2, xor_1_out, xor_2_out);
  xor xor_6 (xor_6_out, xor_3_out, xor_4_out);
  xor xor_7 (out_15, xor_6_out, P);

  assign out_11 = in_4;
  assign out_12 = in_3;
  assign out_13 = in_2;
  assign out_14 = in_1;

  // Notes on the sheet:
  //   Gerador
  //   Validador
endmodule

module _2 (
  input  A1,
  input  A2,
  input  B1,
  input  B2,
  output out_5
);

  wire xnor_1_out, xnor_2_out;

  xnor xnor_1 (xnor_1_out, A1, B1);
  xnor xnor_2 (xnor_2_out, A2, B2);
  xnor xnor_3 (out_5, xnor_1_out, xnor_2_out);
endmodule

module _3 (
  input  A,
  input  B,
  output out_3
);

  wire and_1_out, and_2_out, not_1_out, not_2_out;

  not not_1 (not_1_out, A);
  not not_2 (not_2_out, B);
  and and_1 (and_1_out, not_1_out, B);
  and and_2 (and_2_out, not_2_out, A);
  or or_1 (out_3, and_1_out, and_2_out);
endmodule

module _4 (
  input  A3,
  input  A2,
  input  A1,
  input  A0,
  output out_5
);

  wire and_1_out, and_2_out, not_1_out;

  not not_1 (not_1_out, A3);
  and and_1 (and_1_out, not_1_out, A2);
  and and_2 (and_2_out, not_1_out, A1, A0);
  or or_1 (out_5, and_1_out, and_2_out);
endmodule
