// Logisim project lista_06.circ as structural Verilog
module _1 (
  input  in_1,
  input  in_2,
  input  in_3,
  input  in_4,
  input  in_5,
  output out_6
);

  wire and_1_out, and_2_out;

  and and_1 (and_1_out, in_1, in_2);
  and and_2 (and_2_out, in_3, in_4);
  and and_3 (out_6, and_1_out, in_5, and_2_out);

  // Notes on the sheet:
  //   MUX
endmodule

module _2 (
  input  in_1,
  input  in_2,
  output out_3,
  output out_4,
  output out_5,
  output out_6
);

  and and_1 (out_3, in_1, in_2);

  assign out_4 = out_3;
  assign out_5 = out_3;
  assign out_6 = out_3;

  // Notes on the sheet:
  //   DEMUXER
endmodule

module _3 (
  input  in_1,
  input  in_2,
  input  in_3,
  input  [1:0] in_4,
  input  in_5,
  output out_6
);

  wire [1:0] undriven_5;
  wire [1:1] multiplexer_1_out, undriven, undriven_2, undriven_3, undriven_4;

  Multiplexer #(.select(2), .width(2)) multiplexer_1 (
    .in0({undriven[1], in_1}), .in1({undriven_2[1], in_2}), .in2({undriven_4[1], in_3}),
    .in3({undriven_3[1], in_5}), .out({multiplexer_1_out[1], out_6}), .sel(undriven_5));  // open: en
  // Pins of 1 and 2 bits meet at {undriven[1], in_1}
  // Pins of 1 and 2 bits meet at {multiplexer_1_out[1], out_6}
  // Pins of 1 and 2 bits meet at {undriven_2[1], in_2}
  // Pins of 1 and 2 bits meet at {undriven_4[1], in_3}
  // Pins of 1 and 2 bits meet at {undriven_3[1], in_5}
endmodule
