// Logisim project prataica5.circ as structural Verilog: 4 circuits, main circuit somador-completo
module somador_completo (
  input  Cin,
  input  B,
  input  A,
  output S,
  output Cout
);

  wire and_1_out, and_2_out, and_3_out, xor_1_out;

  xor xor_1 (xor_1_out, B, A);
  and and_1 (and_1_out, B, Cin);
  and and_2 (and_2_out, B, A);
  and and_3 (and_3_out, Cin, A);
  xor xor_2 (S, Cin, xor_1_out);
  or or_1 (Cout, and_1_out, and_2_out, and_3_out);
endmodule

module subtrator_completo (
  input  X1,
  input  Y1,
  input  Bin,
  output Dif,
  output Bout
);

  wire and_1_out, and_2_out, and_3_out, not_1_out, not_2_out, xor_1_out;

  not not_1 (not_1_out, X1);
  not not_2 (not_2_out, X1);
  xor xor_1 (xor_1_out, X1, Y1);
  and and_1 (and_1_out, Y1, Bin);
  and and_2 (and_2_out, not_1_out, Bin);
  and and_3 (and_3_out, not_2_out, Y1);
  xor xor_2 (Dif, xor_1_out, Bin);
  or or_1 (Bout, and_1_out, and_2_out, and_3_out);
endmodule

module subtrator_2bits (
  input  X1,
  input  Y1,
  input  X0,
  input  Y0,
  output S1,
  output bout,
  output S0
);

  wire meio_subtratot_1_bout;

  subtrator_completo subtrator_completo_1 (.X1(X1), .Y1(Y1), .Bin(meio_subtratot_1_bout), .Dif(S1), .Bout(bout));
  meio_subtratot meio_subtratot_1 (.X0(X0), .Y0(Y0), .dif(S0), .Bout(meio_subtratot_1_bout));
endmodule

module meio_subtratot (
  input  X0,
  input  Y0,
  output dif,
  output Bout
);

  wire not_1_out;

  not not_1 (not_1_out, X0);
  xor xor_1 (dif, X0, Y0);
  and and_1 (Bout, not_1_out, Y0);
endmodule
